# Fritzing sketch staci (saved by Fritzing 0.8.5b)
breadboards: 1

parts:
  Part1 = Arduino Mega ADK (Rev3)
  Tiny_RTC1 = Tiny RTC

nets:
  5V: Part1.5V, Tiny_RTC1.VCC
  GND: Part1.GND, Tiny_RTC1.GND

notes:
  VCC GND CS RST A0 SDA SCK LED
  1.8TFT SPI 128*160 v1.1 ST7735
  I2C: SCL SDA

custom parts:
  Tiny RTC: Tiny RTC I2C module DS1370Z RTC and AT24C32 EEPROM
